// Digital circuit Handheld Board.dig as structural Verilog
module Handheld_Board (
);

  wire driver_1_out, nst_chip_1_p1, nst_chip_1_p2, nst_chip_1_p3, nst_chip_1_p4, nst_chip_1_p5,
       nst_chip_1_p6, nst_chip_1_p7;

  // NST_Chip nst_chip_1: pin names not known; wires that end beside it: nst_chip_1_p1, nst_chip_1_p2, nst_chip_1_p3, nst_chip_1_p4, nst_chip_1_p5, nst_chip_1_p6, nst_chip_1_p7
  assign driver_1_out = nst_chip_1_p3 ? nst_chip_1_p2 : 1'bz;  // Driver driver_1
  assign nst_chip_1_p1 = ~nst_chip_1_p3 ? driver_1_out : 1'bz;  // DriverInvSel driverinvsel_1
  Board_Memory_Subsystem board_memory_subsystem_1 (
    .Address_Low_Clock(nst_chip_1_p4), .Address_High_Clock(nst_chip_1_p5), .OE(nst_chip_1_p6),
    .WE(nst_chip_1_p7), .Memory_Bus(driver_1_out));
endmodule
